// Logisim project Fsm.circ as structural Verilog: 3 circuits, main circuit fsm
module fsm (
  input  in_1,
  input  [1:0] In,
  output out_3
);

  wire clk;
  wire [1:0] multiplexer_1_out, register_1_q, statetransition_1_t1;

  Clock clock_1 (.out(clk));
  // Probe on multiplexer_1_out
  // Probe on statetransition_1_t1
  StateTransition statetransition_1 (
    .s0(register_1_q[1]), .s1(register_1_q[0]), .i0(In[1]), .i1(In[0]), .t0(statetransition_1_t1[1]),
    .t1(statetransition_1_t1[0]));
  Register #(.width(2)) register_1 (.D(multiplexer_1_out), .Q(register_1_q), .clk(clk));  // open: en, clr
  Multiplexer #(.width(2)) multiplexer_1 (
    .in0(statetransition_1_t1), .in1(2'b00), .out(multiplexer_1_out), .sel(in_1));  // open: en
  // Probe on register_1_q
  StateOutput stateoutput_1 (.S0(register_1_q[1]), .S1(register_1_q[0]), .I1(In[1]), .I2(In[0]), .Output(out_3));

  // Other names for the same wires on the sheet: CLR = in_1
endmodule

module StateOutput (
  input  S0,
  input  S1,
  input  I1,
  input  I2,
  output Output
);

  wire not_1_out, not_2_out;

  not not_1 (not_1_out, S1);
  and and_1 (Output, S0, not_1_out, not_2_out);
  not not_2 (not_2_out, I2);
endmodule

module StateTransition (
  input  s0,
  input  s1,
  input  i0,
  input  i1,
  output t0,
  output t1
);

  wire and_1_out, and_2_out, and_3_out, and_4_out, not_1_out, not_2_out, not_3_out, not_4_out, not_5_out,
       not_6_out, not_7_out;

  not not_1 (not_1_out, s0);
  and and_1 (and_1_out, not_1_out, s1, not_2_out);
  not not_2 (not_2_out, i1);
  not not_3 (not_3_out, s1);
  and and_2 (and_2_out, s0, not_3_out, not_4_out);
  not not_4 (not_4_out, i1);
  not not_5 (not_5_out, i0);
  and and_3 (and_3_out, not_5_out, i1);
  and and_4 (and_4_out, s0, not_6_out, not_7_out);
  not not_6 (not_6_out, s1);
  not not_7 (not_7_out, i1);
  or or_1 (t0, and_1_out, and_2_out);
  or or_2 (t1, and_3_out, and_4_out);
endmodule
