// Logisim project GRF.circ as structural Verilog: 1 circuit, main circuit grf
module grf (
  input  in_1,
  input  in_2,
  input  in_3,
  input  [4:0] in_4,
  input  [4:0] in_5,
  input  [4:0] in_6,
  input  [31:0] in_7,
  output [31:0] out_8,
  output [31:0] out_9
);

  wire [31:0] r0_out, r1_in, r1_out, r2_in, r2_out, r3_in, r3_out, r4_in, r4_out, r5_in, r5_out, r6_in,
       r6_out, r7_in, r7_out, r8_in, r8_out, r9_in, r9_out, r10_in, r10_out, r11_in, r11_out, r12_in,
       r12_out, r13_in, r13_out, r14_in, r14_out, r15_in, r15_out, r16_in, r16_out, r17_in, r17_out, r18_in,
       r18_out, r19_in, r19_out, r20_in, r20_out, r21_in, r21_out, r22_in, r22_out, r23_in, r23_out, r24_in,
       r24_out, r25_in, r25_out, r26_in, r26_out, r27_in, r27_out, r28_in, r28_out, r29_in, r29_out, r30_in,
       r30_out, r31_in, r31_out;

  // Probe on in_4
  Register #(.width(32)) register_1 (.D({32{1'b0}}), .Q(r0_out), .clk(in_1), .clr(in_3));  // open: en
  Register #(.width(32)) register_2 (.D(r1_in), .Q(r1_out), .clk(in_1), .clr(in_3));  // open: en
  Register #(.width(32)) register_3 (.D(r2_in), .Q(r2_out), .clk(in_1), .clr(in_3));  // open: en
  Register #(.width(32)) register_4 (.D(r3_in), .Q(r3_out), .clk(in_1), .clr(in_3));  // open: en
  Demultiplexer #(.select(5), .width(32), .tristate("true")) demultiplexer_1 (
    .out1(r1_in), .out2(r2_in), .out3(r3_in), .out4(r4_in), .out5(r5_in), .out6(r6_in), .out7(r7_in),
    .out8(r8_in), .out9(r9_in), .out10(r10_in), .out11(r11_in), .out12(r12_in), .out13(r13_in),
    .out14(r14_in), .out15(r15_in), .out16(r16_in), .out17(r17_in), .out18(r18_in), .out19(r19_in),
    .out20(r20_in), .out21(r21_in), .out22(r22_in), .out23(r23_in), .out24(r24_in), .out25(r25_in),
    .out26(r26_in), .out27(r27_in), .out28(r28_in), .out29(r29_in), .out30(r30_in), .out31(r31_in),
    .in(in_7), .sel(in_6), .en(in_2));  // open: out0
  Register #(.width(32)) register_5 (.D(r4_in), .Q(r4_out), .clk(in_1), .clr(in_3));  // open: en
  Register #(.width(32)) register_6 (.D(r5_in), .Q(r5_out), .clk(in_1), .clr(in_3));  // open: en
  Register #(.width(32)) register_7 (.D(r6_in), .Q(r6_out), .clk(in_1), .clr(in_3));  // open: en
  Register #(.width(32)) register_8 (.D(r7_in), .Q(r7_out), .clk(in_1), .clr(in_3));  // open: en
  Register #(.width(32)) register_9 (.D(r8_in), .Q(r8_out), .clk(in_1), .clr(in_3));  // open: en
  Register #(.width(32)) register_10 (.D(r9_in), .Q(r9_out), .clk(in_1), .clr(in_3));  // open: en
  Register #(.width(32)) register_11 (.D(r10_in), .Q(r10_out), .clk(in_1), .clr(in_3));  // open: en
  Register #(.width(32)) register_12 (.D(r11_in), .Q(r11_out), .clk(in_1), .clr(in_3));  // open: en
  Register #(.width(32)) register_13 (.D(r12_in), .Q(r12_out), .clk(in_1), .clr(in_3));  // open: en
  Register #(.width(32)) register_14 (.D(r13_in), .Q(r13_out), .clk(in_1), .clr(in_3));  // open: en
  Register #(.width(32)) register_15 (.D(r14_in), .Q(r14_out), .clk(in_1), .clr(in_3));  // open: en
  Register #(.width(32)) register_16 (.D(r15_in), .Q(r15_out), .clk(in_1), .clr(in_3));  // open: en
  Register #(.width(32)) register_17 (.D(r16_in), .Q(r16_out), .clk(in_1), .clr(in_3));  // open: en
  Register #(.width(32)) register_18 (.D(r17_in), .Q(r17_out), .clk(in_1), .clr(in_3));  // open: en
  Register #(.width(32)) register_19 (.D(r18_in), .Q(r18_out), .clk(in_1), .clr(in_3));  // open: en
  Register #(.width(32)) register_20 (.D(r19_in), .Q(r19_out), .clk(in_1), .clr(in_3));  // open: en
  Multiplexer #(.select(5), .width(32), .disabled(0)) multiplexer_1 (
    .in0(r0_out), .in1(r1_out), .in2(r2_out), .in3(r3_out), .in4(r4_out), .in5(r5_out), .in6(r6_out),
    .in7(r7_out), .in8(r8_out), .in9(r9_out), .in10(r10_out), .in11(r11_out), .in12(r12_out), .in13(r13_out),
    .in14(r14_out), .in15(r15_out), .in16(r16_out), .in17(r17_out), .in18(r18_out), .in19(r19_out),
    .in20(r20_out), .in21(r21_out), .in22(r22_out), .in23(r23_out), .in24(r24_out), .in25(r25_out),
    .in26(r26_out), .in27(r27_out), .in28(r28_out), .in29(r29_out), .in30(r30_out), .in31(r31_out),
    .out(out_8), .sel(in_4), .en(1'b1));
  Multiplexer #(.select(5), .width(32), .disabled(0)) multiplexer_2 (
    .in0(r0_out), .in1(r1_out), .in2(r2_out), .in3(r3_out), .in4(r4_out), .in5(r5_out), .in6(r6_out),
    .in7(r7_out), .in8(r8_out), .in9(r9_out), .in10(r10_out), .in11(r11_out), .in12(r12_out), .in13(r13_out),
    .in14(r14_out), .in15(r15_out), .in16(r16_out), .in17(r17_out), .in18(r18_out), .in19(r19_out),
    .in20(r20_out), .in21(r21_out), .in22(r22_out), .in23(r23_out), .in24(r24_out), .in25(r25_out),
    .in26(r26_out), .in27(r27_out), .in28(r28_out), .in29(r29_out), .in30(r30_out), .in31(r31_out),
    .out(out_9), .sel(in_5), .en(1'b1));
  Register #(.width(32)) register_21 (.D(r20_in), .Q(r20_out), .clk(in_1), .clr(in_3));  // open: en
  Register #(.width(32)) register_22 (.D(r21_in), .Q(r21_out), .clk(in_1), .clr(in_3));  // open: en
  Register #(.width(32)) register_23 (.D(r22_in), .Q(r22_out), .clk(in_1), .clr(in_3));  // open: en
  Register #(.width(32)) register_24 (.D(r23_in), .Q(r23_out), .clk(in_1), .clr(in_3));  // open: en
  Register #(.width(32)) register_25 (.D(r24_in), .Q(r24_out), .clk(in_1), .clr(in_3));  // open: en
  Register #(.width(32)) register_26 (.D(r25_in), .Q(r25_out), .clk(in_1), .clr(in_3));  // open: en
  Register #(.width(32)) register_27 (.D(r26_in), .Q(r26_out), .clk(in_1), .clr(in_3));  // open: en
  Register #(.width(32)) register_28 (.D(r27_in), .Q(r27_out), .clk(in_1), .clr(in_3));  // open: en
  // Probe on nothing
  Register #(.width(32)) register_29 (.D(r28_in), .Q(r28_out), .clk(in_1), .clr(in_3));  // open: en
  Register #(.width(32)) register_30 (.D(r29_in), .Q(r29_out), .clk(in_1), .clr(in_3));  // open: en
  Register #(.width(32)) register_31 (.D(r30_in), .Q(r30_out), .clk(in_1), .clr(in_3));  // open: en
  Register #(.width(32)) register_32 (.D(r31_in), .Q(r31_out), .clk(in_1), .clr(in_3));  // open: en

  // Other names for the same wires on the sheet: A1[4:0] = in_4; A2[4:0] = in_5; A3[4:0] = in_6; clk = in_1;
  //   clr = in_3; WD[31:0] = in_7; WE = in_2
endmodule
