// Logisim project ftoi.circ as structural Verilog: 3 circuits, main circuit ftoi
module ftoi (
  input  [15:0] in_1,
  output [31:0] \int 
);

  wire [1:0] select;
  wire [4:0] NewE;
  wire [10:0] bit_extender_1_out;
  wire [31:0] NewM, solve_1_out_4;

  Solve solve_1 (.E(NewE), .Sign(in_1[15]), .in_3(NewM), .out_4(solve_1_out_4));
  // Probe on in_1[9:0]
  // Probe on in_1[14:10]
  Multiplexer #(.select(2), .width(32)) multiplexer_1 (
    .in0(solve_1_out_4), .in1({32{1'b0}}), .in2({32{1'b0}}), .out(\int ), .sel(select));  // open: in3, en
  assign bit_extender_1_out = {{1{1'b1}}, in_1[9:0]};  // Bit_Extender bit_extender_1
  // Probe on select
  ClassifyE classifye_1 (.E(in_1[14:10]), .\type (select), .out_3(NewE));
  // Probe on NewE
  // Probe on bit_extender_1_out
  assign NewM = {{21{1'b0}}, bit_extender_1_out};  // Bit_Extender bit_extender_2
  // Probe on NewM

  // Other names for the same wires on the sheet: float[15:0] = in_1; M[9:0] = in_1[9:0]; E[4:0] = in_1[14:10];
  //   S = in_1[15]
endmodule

module ClassifyE (
  input  [4:0] E,
  output [1:0] \type ,
  output [4:0] out_3
);

  wire comparator_1_eq, type_t;
  wire [1:0] multiplexer_1_out;

  Comparator #(.width(5), .mode("unsigned")) comparator_1 (.a(E), .b({5{1'b1}}), .eq(comparator_1_eq));  // open: gt, lt
  Multiplexer #(.width(2)) multiplexer_1 (.in0(2'b00), .in1(2'b01), .out(multiplexer_1_out), .sel(type_t));  // open: en
  Comparator #(.width(5), .mode("unsigned")) comparator_2 (.a(E), .b({5{1'b0}}), .eq(type_t));  // open: gt, lt
  Multiplexer #(.width(2)) multiplexer_2 (
    .in0(multiplexer_1_out), .in1(2'b10), .out(\type ), .sel(comparator_1_eq));  // open: en
  Subtractor #(.width(5)) subtractor_1 (.a(E), .b(5'b01111), .out(out_3));  // open: bin, bout
endmodule

module Solve (
  input  [4:0] E,
  input  Sign,
  input  [31:0] in_3,
  output [31:0] out_4
);

  wire comparator_1_gt, comparator_2_eq;
  wire [31:0] _0ornot, adder_1_out, extend, not_1_out, Out, t, tmp;

  Shifter #(.width(32), .shift("lr")) shifter_1 (.in(t), .\dist (5'b01010), .out(extend));
  Comparator #(.width(5)) comparator_1 (.a(E), .b({5{1'b0}}), .gt(comparator_1_gt));  // open: eq, lt
  Comparator #(.width(5), .mode("unsigned")) comparator_2 (.a(E), .b({5{1'b0}}), .eq(comparator_2_eq));  // open: gt, lt
  Multiplexer #(.width(32)) multiplexer_1 (.in0(32'h1), .in1({32{1'b1}}), .out(tmp), .sel(Sign));  // open: en
  Shifter #(.width(32)) shifter_2 (.in(in_3), .\dist (E), .out(t));
  // Probe on t
  // Probe on out_4
  Multiplexer #(.width(32)) multiplexer_2 (.in0(_0ornot), .in1(Out), .out(out_4), .sel(comparator_1_gt));  // open: en
  Multiplexer #(.width(32)) multiplexer_3 (
    .in0({32{1'b0}}), .in1(tmp), .out(_0ornot), .sel(comparator_2_eq));  // open: en
  assign not_1_out = ~extend;  // NOT_Gate not_1, 32 bits wide
  Adder #(.width(32)) adder_1 (.a(not_1_out), .b(32'h1), .out(adder_1_out));  // open: cin, cout
  Multiplexer #(.width(32)) multiplexer_4 (.in0(extend), .in1(adder_1_out), .out(Out), .sel(Sign));  // open: en

  // Other names for the same wires on the sheet: S = Sign
endmodule
