// Logisim project CRC.circ as structural Verilog: 2 circuits, main circuit CRC
module CRC (
  input  [7:0] Origin,
  input  [3:0] divisor,
  output [10:0] C
);

  wire [3:1] t1, t2, t3, t4, t5, t6, t7;

  mod2divide mod2divide_1 (.dividend({t1, Origin[3]}), .divisor(divisor), .quotient(t2));
  mod2divide mod2divide_2 (.dividend({t3, Origin[1]}), .divisor(divisor), .quotient(t4));
  mod2divide mod2divide_3 (.dividend({t5, 1'b0}), .divisor(divisor), .quotient(t6));
  mod2divide mod2divide_4 (.dividend({t7, 1'b0}), .divisor(divisor), .quotient(C[2:0]));
  // Probe on {Origin, 3'b000}
  // Probe on Origin[7:4]
  mod2divide mod2divide_5 (.dividend(Origin[7:4]), .divisor(divisor), .quotient(t1));
  // Probe on t1
  mod2divide mod2divide_6 (.dividend({t2, Origin[2]}), .divisor(divisor), .quotient(t3));
  mod2divide mod2divide_7 (.dividend({t4, Origin[0]}), .divisor(divisor), .quotient(t5));
  mod2divide mod2divide_8 (.dividend({t6, 1'b0}), .divisor(divisor), .quotient(t7));
  // Probe on {t1, Origin[3]}

  assign C[10:3] = Origin;

  // Other names for the same wires on the sheet: _3 = Origin[0]; t4[0] = Origin[0]; _5 = Origin[2]; t2[0] = Origin[2];
  //   _6 = Origin[3]; t1[0] = Origin[3]; _4 = Origin[1]; t3[0] = Origin[1]
endmodule

module mod2divide (
  input  [3:0] dividend,
  input  [3:0] divisor,
  output [2:0] quotient
);

  wire comparator_1_eq;
  wire [3:0] multiplexer_1_out, shifter_1_out, xor_1_out;

  Shifter #(.width(4), .shift("lr")) shifter_1 (.in(dividend), .\dist (2'b11), .out(shifter_1_out));
  // Probe on shifter_1_out
  Comparator #(.width(4), .mode("unsigned")) comparator_1 (
    .a(shifter_1_out), .b(4'b0000), .eq(comparator_1_eq));  // open: gt, lt
  // Probe on multiplexer_1_out
  Multiplexer #(.width(4)) multiplexer_1 (
    .in0(divisor), .in1(4'b0000), .out(multiplexer_1_out), .sel(comparator_1_eq));  // open: en
  // Probe on dividend
  // Probe on xor_1_out
  assign xor_1_out = multiplexer_1_out ^ dividend;  // XOR_Gate xor_1, 4 bits wide
  Bit_Extender #(.in_width(4), .out_width(3)) bit_extender_1 (.in(xor_1_out), .out(quotient));
endmodule
