// Logisim project navi.circ as structural Verilog: 3 circuits, main circuit StateOuput
module navigation (
  input  [1:0] in_1,
  input  in_2,
  input  in_3,
  output arrive,
  output fit
);

  wire comparator_1_eq, multiplexer_1_out;
  wire [2:0] register_1_q, statetranmition_1_t0;

  Clock clock_1 ();  // open: out
  // Probe on register_1_q
  StateTranmition statetranmition_1 (
    .S2(register_1_q[2]), .S1(register_1_q[1]), .S0(register_1_q[0]), .d1(in_1[1]), .d0(in_1[0]),
    .t2(statetranmition_1_t0[2]), .t1(statetranmition_1_t0[1]), .t0(statetranmition_1_t0[0]));
  // Probe on statetranmition_1_t0
  Register #(.width(3)) register_1 (.D(statetranmition_1_t0), .Q(register_1_q), .clk(in_2), .clr(in_3));  // open: en
  Comparator #(.width(3), .mode("unsigned")) comparator_1 (
    .a(statetranmition_1_t0), .b(register_1_q), .eq(comparator_1_eq));  // open: gt, lt
  // Probe on register_1_q
  Multiplexer multiplexer_1 (.in0(1'b0), .in1(1'b1), .out(multiplexer_1_out), .sel(comparator_1_eq));  // open: en
  StateOuput stateouput_1 (.S2(register_1_q[2]), .S1(register_1_q[1]), .S0(register_1_q[0]), .A(arrive));
  Register #(.width(1)) register_2 (.D(multiplexer_1_out), .Q(fit), .clk(in_2), .clr(in_3));  // open: en

  // Other names for the same wires on the sheet: clk = in_2; dir[1:0] = in_1; reset = in_3
endmodule

module StateOuput (
  input  S2,
  input  S1,
  input  S0,
  output A
);

  wire not_1_out, not_2_out;

  not not_1 (not_1_out, S1);
  not not_2 (not_2_out, S0);
  and and_1 (A, S2, not_1_out, not_2_out);
endmodule

module StateTranmition (
  input  S2,
  input  S1,
  input  S0,
  input  d1,
  input  d0,
  output t2,
  output t1,
  output t0
);

  wire and_1_out, and_2_out, and_3_out, and_4_out, and_5_out, and_6_out, and_7_out, and_8_out, and_9_out,
       and_10_out, and_11_out, not_1_out, not_2_out, not_3_out, not_4_out, not_5_out, not_6_out, not_7_out,
       not_8_out, not_9_out, not_10_out, not_11_out, not_12_out, not_13_out, not_14_out, not_15_out,
       not_16_out, not_17_out;

  not not_1 (not_1_out, S0);
  not not_2 (not_2_out, d1);
  not not_3 (not_3_out, d0);
  not not_4 (not_4_out, d1);
  not not_5 (not_5_out, S1);
  not not_6 (not_6_out, d1);
  not not_7 (not_7_out, d1);
  not not_8 (not_8_out, d0);
  not not_9 (not_9_out, S0);
  not not_10 (not_10_out, d1);
  not not_11 (not_11_out, S0);
  not not_12 (not_12_out, d0);
  not not_13 (not_13_out, S2);
  not not_14 (not_14_out, S1);
  not not_15 (not_15_out, d1);
  not not_16 (not_16_out, d0);
  not not_17 (not_17_out, d0);
  and and_1 (and_1_out, S1, not_1_out, not_2_out, not_3_out);
  and and_2 (and_2_out, S1, S0, not_4_out, d0);
  and and_3 (and_3_out, not_5_out, S0, not_6_out);
  and and_4 (and_4_out, S0, not_7_out, not_8_out);
  and and_5 (and_5_out, S1, not_9_out, not_10_out, d0);
  and and_6 (and_6_out, S1, not_11_out, d1, not_12_out);
  and and_7 (and_7_out, S1, S0, d1, d0);
  and and_8 (and_8_out, not_13_out, not_14_out, not_15_out, not_16_out);
  and and_9 (and_9_out, S0, d1, d0);
  and and_10 (and_10_out, S1, d1, d0);
  and and_11 (and_11_out, S1, S0, not_17_out);
  or or_1 (t2, and_1_out, and_2_out);
  or or_2 (t1, and_3_out, and_4_out, and_5_out, and_6_out, and_7_out);
  or or_3 (t0, and_8_out, and_9_out, and_10_out, and_11_out);
endmodule
