// Logisim project Cpu.circ as structural Verilog: 8 circuits, main circuit main
module main (
  input  reset,
  output [31:0] instr,
  output RegWrite,
  output [4:0] RegAddress,
  output [31:0] RegData,
  output MemWrite,
  output [4:0] MemAddress,
  output [31:0] MemData
);

  wire AluSrc, beq, clk, j_jal, jal, jr, RegDst, SignExt, undriven, Zero;
  wire [1:0] WhichtoReg;
  wire [2:0] AluOp;
  wire [4:0] multiplexer_2_out;
  wire [31:0] imm32, MemRead, multiplexer_1_out, PC_4, PC_jr, RD1, res;

  // Probe on instr[15:0]
  Clock clock_1 (.out(clk));
  // Probe on instr
  EXT EXT (.imm16(instr[15:0]), .Imm32(imm32), .in_1(SignExt));
  // Probe on instr
  IFU_asynchronous_jtype ifu_asynchronous_jtype_1 (
    .in_1(reset), .in_2(clk), .in_3(beq), .in_4(Zero), .in_5(j_jal), .in_6(jr), .in_7(imm32), .in_8(RD1),
    .out_9(instr), .out_10(PC_4));
  Control control_1 (
    .op(instr[31:26]), .func(instr[5:0]), .AluOp(AluOp), .RegWrite(RegWrite), .MemWrite(MemWrite), .beq(beq),
    .AluSrc(AluSrc), .WhichtoReg(WhichtoReg), .RegDst(RegDst), .SignExt(SignExt), .j_jal(j_jal), .jal(jal),
    .jr(jr));
  Multiplexer #(.width(32)) multiplexer_1 (
    .in0(MemData), .in1(imm32), .out(multiplexer_1_out), .sel(AluSrc), .en(undriven));
  // Probe on SignExt
  // Probe on instr[15:11]
  // Probe on instr[20:16]
  // Probe on instr[20:16]
  ALU ALU (
    .SrcA(RD1), .out_6({res[31:7], MemAddress, res[1:0]}), .SrcB(multiplexer_1_out), .in_1(AluOp),
    .out_5(Zero), .shamt(instr[10:6]));
  // Probe on instr[25:21]
  Multiplexer #(.width(5), .enable("false")) multiplexer_2 (
    .in0(instr[15:11]), .in1(instr[20:16]), .out(multiplexer_2_out), .sel(RegDst));
  // Probe on RegAddress
  Multiplexer #(.width(5)) multiplexer_3 (
    .in0(multiplexer_2_out), .in1({5{1'b1}}), .out(RegAddress), .sel(jal));  // open: en
  Multiplexer #(.select(2), .width(32), .enable("false")) multiplexer_4 (
    .in0({res[31:7], MemAddress, res[1:0]}), .in1(MemRead), .in2({instr[15:0], {16{1'b0}}}), .in3(PC_4),
    .out(RegData), .sel(WhichtoReg));
  // Probe on WhichtoReg
  DM dm_1 (.A(MemAddress), .in_5(MemData), .in_1(MemWrite), .in_2(reset), .in_3(clk), .ReadData(MemRead));
  GRF grf_1 (
    .in_4(instr[25:21]), .in_5(instr[20:16]), .in_6(RegAddress), .in_7(RegData), .out_8(RD1),
    .out_9(MemData), .in_1(clk), .in_3(reset), .in_2(RegWrite), .out_10(PC_jr));
  // Probe on RegData

  // Other names for the same wires on the sheet: func[5:0] = instr[5:0]; imm16[15:0] = instr[15:0];
  //   shamt[4:0] = instr[10:6]; Rd[4:0] = instr[15:11]; Rt[4:0] = instr[20:16]; Rs[4:0] = instr[25:21];
  //   op[5:0] = instr[31:26]; RD2[31:0] = MemData; res[6:2] = MemAddress

  // Notes on the sheet:
  //   11.9 更新
  //   增加j, jal, jr指令
  //   SrcA
  //   DM
endmodule

module GRF (
  input  in_1,
  input  in_2,
  input  in_3,
  input  [4:0] in_4,
  input  [4:0] in_5,
  input  [4:0] in_6,
  input  [31:0] in_7,
  output [31:0] out_8,
  output [31:0] out_9,
  output [31:0] out_10
);

  wire [31:0] r0_out, r1_in, r1_out, r2_in, r2_out, r3_in, r3_out, r4_in, r4_out, r5_in, r5_out, r6_in,
       r6_out, r7_in, r7_out, r8_in, r8_out, r9_in, r9_out, r10_in, r10_out, r11_in, r11_out, r12_in,
       r12_out, r13_in, r13_out, r14_in, r14_out, r15_in, r15_out, r16_in, r16_out, r17_in, r17_out, r18_in,
       r18_out, r19_in, r19_out, r20_in, r20_out, r21_in, r21_out, r22_in, r22_out, r23_in, r23_out, r24_in,
       r24_out, r25_in, r25_out, r26_in, r26_out, r27_in, r27_out, r28_in, r28_out, r29_in, r29_out, r30_in,
       r30_out, r31_in;

  // Probe on in_4
  Register #(.width(32)) register_1 (.D({32{1'b0}}), .Q(r0_out), .clk(in_1), .clr(in_3));  // open: en
  Register #(.width(32)) register_2 (.D(r1_in), .Q(r1_out), .clk(in_1), .clr(in_3));  // open: en
  Register #(.width(32)) register_3 (.D(r2_in), .Q(r2_out), .clk(in_1), .clr(in_3));  // open: en
  Register #(.width(32)) register_4 (.D(r3_in), .Q(r3_out), .clk(in_1), .clr(in_3));  // open: en
  Demultiplexer #(.select(5), .width(32), .tristate("true")) demultiplexer_1 (
    .out1(r1_in), .out2(r2_in), .out3(r3_in), .out4(r4_in), .out5(r5_in), .out6(r6_in), .out7(r7_in),
    .out8(r8_in), .out9(r9_in), .out10(r10_in), .out11(r11_in), .out12(r12_in), .out13(r13_in),
    .out14(r14_in), .out15(r15_in), .out16(r16_in), .out17(r17_in), .out18(r18_in), .out19(r19_in),
    .out20(r20_in), .out21(r21_in), .out22(r22_in), .out23(r23_in), .out24(r24_in), .out25(r25_in),
    .out26(r26_in), .out27(r27_in), .out28(r28_in), .out29(r29_in), .out30(r30_in), .out31(r31_in),
    .in(in_7), .sel(in_6), .en(in_2));  // open: out0
  Register #(.width(32)) register_5 (.D(r4_in), .Q(r4_out), .clk(in_1), .clr(in_3));  // open: en
  Register #(.width(32)) register_6 (.D(r5_in), .Q(r5_out), .clk(in_1), .clr(in_3));  // open: en
  Register #(.width(32)) register_7 (.D(r6_in), .Q(r6_out), .clk(in_1), .clr(in_3));  // open: en
  Register #(.width(32)) register_8 (.D(r7_in), .Q(r7_out), .clk(in_1), .clr(in_3));  // open: en
  Register #(.width(32)) register_9 (.D(r8_in), .Q(r8_out), .clk(in_1), .clr(in_3));  // open: en
  Register #(.width(32)) register_10 (.D(r9_in), .Q(r9_out), .clk(in_1), .clr(in_3));  // open: en
  Register #(.width(32)) register_11 (.D(r10_in), .Q(r10_out), .clk(in_1), .clr(in_3));  // open: en
  Register #(.width(32)) register_12 (.D(r11_in), .Q(r11_out), .clk(in_1), .clr(in_3));  // open: en
  Register #(.width(32)) register_13 (.D(r12_in), .Q(r12_out), .clk(in_1), .clr(in_3));  // open: en
  Register #(.width(32)) register_14 (.D(r13_in), .Q(r13_out), .clk(in_1), .clr(in_3));  // open: en
  Register #(.width(32)) register_15 (.D(r14_in), .Q(r14_out), .clk(in_1), .clr(in_3));  // open: en
  Register #(.width(32)) register_16 (.D(r15_in), .Q(r15_out), .clk(in_1), .clr(in_3));  // open: en
  Register #(.width(32)) register_17 (.D(r16_in), .Q(r16_out), .clk(in_1), .clr(in_3));  // open: en
  Register #(.width(32)) register_18 (.D(r17_in), .Q(r17_out), .clk(in_1), .clr(in_3));  // open: en
  Register #(.width(32)) register_19 (.D(r18_in), .Q(r18_out), .clk(in_1), .clr(in_3));  // open: en
  Register #(.width(32)) register_20 (.D(r19_in), .Q(r19_out), .clk(in_1), .clr(in_3));  // open: en
  Multiplexer #(.select(5), .width(32), .disabled(0)) multiplexer_1 (
    .in0(r0_out), .in1(r1_out), .in2(r2_out), .in3(r3_out), .in4(r4_out), .in5(r5_out), .in6(r6_out),
    .in7(r7_out), .in8(r8_out), .in9(r9_out), .in10(r10_out), .in11(r11_out), .in12(r12_out), .in13(r13_out),
    .in14(r14_out), .in15(r15_out), .in16(r16_out), .in17(r17_out), .in18(r18_out), .in19(r19_out),
    .in20(r20_out), .in21(r21_out), .in22(r22_out), .in23(r23_out), .in24(r24_out), .in25(r25_out),
    .in26(r26_out), .in27(r27_out), .in28(r28_out), .in29(r29_out), .in30(r30_out), .in31(out_10),
    .out(out_8), .sel(in_4), .en(1'b1));
  Multiplexer #(.select(5), .width(32), .disabled(0)) multiplexer_2 (
    .in0(r0_out), .in1(r1_out), .in2(r2_out), .in3(r3_out), .in4(r4_out), .in5(r5_out), .in6(r6_out),
    .in7(r7_out), .in8(r8_out), .in9(r9_out), .in10(r10_out), .in11(r11_out), .in12(r12_out), .in13(r13_out),
    .in14(r14_out), .in15(r15_out), .in16(r16_out), .in17(r17_out), .in18(r18_out), .in19(r19_out),
    .in20(r20_out), .in21(r21_out), .in22(r22_out), .in23(r23_out), .in24(r24_out), .in25(r25_out),
    .in26(r26_out), .in27(r27_out), .in28(r28_out), .in29(r29_out), .in30(r30_out), .in31(out_10),
    .out(out_9), .sel(in_5), .en(1'b1));
  Register #(.width(32)) register_21 (.D(r20_in), .Q(r20_out), .clk(in_1), .clr(in_3));  // open: en
  Register #(.width(32)) register_22 (.D(r21_in), .Q(r21_out), .clk(in_1), .clr(in_3));  // open: en
  Register #(.width(32)) register_23 (.D(r22_in), .Q(r22_out), .clk(in_1), .clr(in_3));  // open: en
  Register #(.width(32)) register_24 (.D(r23_in), .Q(r23_out), .clk(in_1), .clr(in_3));  // open: en
  Register #(.width(32)) register_25 (.D(r24_in), .Q(r24_out), .clk(in_1), .clr(in_3));  // open: en
  Register #(.width(32)) register_26 (.D(r25_in), .Q(r25_out), .clk(in_1), .clr(in_3));  // open: en
  Register #(.width(32)) register_27 (.D(r26_in), .Q(r26_out), .clk(in_1), .clr(in_3));  // open: en
  Register #(.width(32)) register_28 (.D(r27_in), .Q(r27_out), .clk(in_1), .clr(in_3));  // open: en
  Register #(.width(32)) register_29 (.D(r28_in), .Q(r28_out), .clk(in_1), .clr(in_3));  // open: en
  Register #(.width(32)) register_30 (.D(r29_in), .Q(r29_out), .clk(in_1), .clr(in_3));  // open: en
  Register #(.width(32)) register_31 (.D(r30_in), .Q(r30_out), .clk(in_1), .clr(in_3));  // open: en
  Register #(.width(32)) register_32 (.D(r31_in), .Q(out_10), .clk(in_1), .clr(in_3));  // open: en

  // Other names for the same wires on the sheet: A1[4:0] = in_4; A2[4:0] = in_5; A3[4:0] = in_6; clk = in_1;
  //   clr = in_3; r31_out[31:0] = out_10; WD[31:0] = in_7; WE = in_2
endmodule

module ALU (
  input  [2:0] in_1,
  input  [31:0] SrcA,
  input  [31:0] SrcB,
  input  [4:0] shamt,
  output out_5,
  output [31:0] out_6
);

  wire [31:0] adder_1_out, AND_out, OR_out, shifter_1_out, subtractor_1_out;

  Shifter #(.width(32)) shifter_1 (.in(SrcB), .\dist (shamt), .out(shifter_1_out));
  Adder #(.width(32)) adder_1 (.a(SrcA), .b(SrcB), .out(adder_1_out));  // open: cin, cout
  Subtractor #(.width(32)) subtractor_1 (.a(SrcA), .b(SrcB), .out(subtractor_1_out));  // open: bin, bout
  assign AND_out = SrcA & SrcB;  // AND_Gate AND, 32 bits wide
  assign OR_out = SrcA | SrcB;  // OR_Gate OR, 32 bits wide
  Multiplexer #(.select(3), .width(32)) multiplexer_1 (
    .in0(adder_1_out), .in1(subtractor_1_out), .in2(AND_out), .in3(OR_out), .in4(shifter_1_out), .out(out_6),
    .sel(in_1));  // open: in5, in6, in7, en
  // Probe on out_6
  Comparator #(.width(32), .mode("unsigned")) comparator_1 (.a(SrcA), .b(SrcB), .eq(out_5));  // open: gt, lt

  // Other names for the same wires on the sheet: ALUOp[2:0] = in_1; ALUResult[31:0] = out_6

  // Notes on the sheet:
  //   000 +
  //   001 -
  //   010 and
  //   011 or
endmodule

module EXT (
  input  in_1,
  input  [15:0] imm16,
  output [31:0] Imm32
);

  wire [31:0] bit_extender_1_out, bit_extender_2_out;

  assign bit_extender_1_out = {{16{1'b0}}, imm16};  // Bit_Extender bit_extender_1
  assign bit_extender_2_out = {{16{imm16[15]}}, imm16};  // Bit_Extender bit_extender_2
  Multiplexer #(.width(32)) multiplexer_1 (
    .in0(bit_extender_1_out), .in1(bit_extender_2_out), .out(Imm32), .sel(in_1));  // open: en

  // Other names for the same wires on the sheet: extOp = in_1

  // Notes on the sheet:
  //   0_extend
endmodule

module DM (
  input  in_1,
  input  in_2,
  input  in_3,
  input  [4:0] A,
  input  [31:0] in_5,
  output [31:0] ReadData
);

  // Probe on in_5
  RAM #(.addrWidth(5), .dataWidth(32), .bus("separate")) ram_1 (
    .addr(A), .din(in_5), .data(ReadData), .str(in_1), .clk(in_3), .clr(in_2));  // open: sel, ld

  // Other names for the same wires on the sheet: Address[4:0] = A; clk = in_3; MemWrite = in_1; Reset = in_2;
  //   WriteData[31:0] = in_5
endmodule

module IFU_asynchronous (
  input  in_1,
  input  in_2,
  input  in_3,
  input  in_4,
  input  [31:0] in_5,
  output [31:0] out_6
);

  wire and_1_out, comparator_1_eq;
  wire [31:0] adder_2_out, NPC, PC, PC_4, PC_q, shifter_1_out, subtractor_1_out;

  Shifter #(.width(32)) shifter_1 (.in(in_5), .\dist (5'b00010), .out(shifter_1_out));
  // Probe on shifter_1_out
  Register #(.width(32)) u_PC (.D(NPC), .Q(PC_q), .clk(in_2), .clr(in_1));  // open: en
  Adder #(.width(32)) adder_1 (.a(PC), .b(32'h4), .out(PC_4));  // open: cin, cout
  Adder #(.width(32)) adder_2 (.a(PC_4), .b(shifter_1_out), .out(adder_2_out));  // open: cin, cout
  Multiplexer #(.width(32), .enable("false")) multiplexer_1 (.in0(PC_4), .in1(adder_2_out), .out(NPC), .sel(and_1_out));
  and and_1 (and_1_out, in_3, in_4);
  Comparator #(.width(32), .mode("unsigned")) comparator_1 (
    .a(PC_q), .b({32{1'b0}}), .eq(comparator_1_eq));  // open: gt, lt
  // Probe on PC
  Multiplexer #(.width(32)) multiplexer_2 (.in0(PC_q), .in1(32'h3000), .out(PC), .sel(comparator_1_eq));  // open: en
  // Probe on subtractor_1_out
  // Probe on subtractor_1_out[6:2]
  Subtractor #(.width(32)) subtractor_1 (.a(PC), .b(32'h3000), .out(subtractor_1_out));  // open: bin, bout
  ROM #(.addrWidth(5), .dataWidth(32)) rom_1 (.addr(subtractor_1_out[6:2]), .data(out_6));  // open: sel
  // Probe on out_6

  // Other names for the same wires on the sheet: beq = in_3; clk = in_2; imm[31:0] = in_5; instr[31:0] = out_6;
  //   Reset = in_1; Zero = in_4

  // Notes on the sheet:
  //   contents of rom_1 (hex, n*v repeats v):
  //   34490330 344a0386 344b044d 12b6021 18a6823 ac0d0004 8c4e0000 3c100454 37180001 37390063 338c821
  //   35ef0064 11f9fffd
endmodule

module Control (
  input  [5:0] op,
  input  [5:0] func,
  output [2:0] AluOp,
  output RegWrite,
  output MemWrite,
  output beq,
  output AluSrc,
  output [1:0] WhichtoReg,
  output RegDst,
  output SignExt,
  output j_jal,
  output jal,
  output jr
);

  wire addu, andi, j, lb, lui, lw, not_1_out, not_2_out, not_3_out, not_4_out, not_5_out, not_6_out,
       not_7_out, not_8_out, not_9_out, not_10_out, not_11_out, not_12_out, ori, R, sll, subu;

  // Probe on op
  not not_1 (not_1_out, op[5]);
  not not_2 (not_2_out, op[3]);
  not not_3 (not_3_out, op[4]);
  not not_4 (not_4_out, op[2]);
  not not_5 (not_5_out, op[0]);
  not not_6 (not_6_out, op[1]);
  // Probe on func
  not not_7 (not_7_out, func[5]);
  not not_8 (not_8_out, func[3]);
  not not_9 (not_9_out, func[4]);
  not not_10 (not_10_out, func[2]);
  not not_11 (not_11_out, func[0]);
  not not_12 (not_12_out, func[1]);
  and u_R (R, not_5_out, not_6_out, not_4_out, not_2_out, not_3_out, not_1_out);
  and u_addu (addu, R, func[0], not_12_out, not_10_out, not_8_out, not_9_out, func[5]);
  and u_subu (subu, R, func[0], func[1], not_10_out, not_8_out, not_9_out, func[5]);
  and u_ori (ori, op[0], not_6_out, op[2], op[3], not_3_out, not_1_out);
  and u_lw (lw, op[0], op[1], not_4_out, not_2_out, not_3_out, op[5]);
  and sw (MemWrite, op[0], op[1], not_4_out, op[3], not_3_out, op[5]);
  and u_beq (beq, not_5_out, not_6_out, op[2], not_2_out, not_3_out, not_1_out);
  and u_lui (lui, op[0], op[1], op[2], op[3], not_3_out, not_1_out);
  and u_j (j, not_5_out, op[1], not_4_out, not_2_out, not_3_out, not_1_out);
  and u_jal (jal, op[0], op[1], not_4_out, not_2_out, not_3_out, not_1_out);
  and u_jr (jr, R, not_11_out, not_12_out, not_10_out, func[3], not_9_out, not_7_out);
  and u_andi (andi, not_1_out, not_3_out, op[3], not_6_out, not_5_out);
  and u_sll (sll, R, not_7_out, not_9_out, not_10_out, not_12_out, not_11_out);
  and u_lb (lb, op[5], not_3_out, not_2_out, not_4_out, not_5_out);
  buf or_1 (AluOp[2], sll);  // OR_Gate
  or or_2 (AluOp[0], subu, ori);
  or or_3 (AluOp[1], ori, andi);
  or or_4 (WhichtoReg[0], jal, lw, lb);
  or or_5 (WhichtoReg[1], jal, lui);
  or or_6 (RegWrite, addu, subu, lw, sll, ori, lui, jal);
  not not_13 (RegDst, R);
  or or_7 (AluSrc, ori, lw, MemWrite);
  or or_8 (SignExt, lw, MemWrite, beq, lb);
  or or_9 (j_jal, j, jal);
  // Probe on AluOp

  // Other names for the same wires on the sheet: sw = MemWrite

  // Notes on the sheet:
  //   0: reg, 1: ext(imm)
  //   00 AluRes->Reg
  //   01 Mem->Reg
  //   10 lui to Reg
  //   0 Rd is the WriteAddr
  //   1 Rt is the WriteAddr
  //   11 PC+4 -> Reg
endmodule

module IFU_asynchronous_jtype (
  input  in_1,
  input  in_2,
  input  in_3,
  input  in_4,
  input  in_5,
  input  in_6,
  input  [31:0] in_7,
  input  [31:0] in_8,
  output [31:0] out_9,
  output [31:0] out_10
);

  wire and_1_out, comparator_1_eq;
  wire [31:0] adder_2_out, multiplexer_1_out, multiplexer_2_out, NPC, PC, PC_q, shifter_1_out,
       subtractor_1_out;

  // Probe on NPC
  Shifter #(.width(32)) shifter_1 (.in(in_7), .\dist (5'b00010), .out(shifter_1_out));
  // Probe on shifter_1_out
  Register #(.width(32)) u_PC (.D(NPC), .Q(PC_q), .clk(in_2), .clr(in_1));  // open: en
  Adder #(.width(32)) adder_1 (.a(PC), .b(32'h4), .out(out_10));  // open: cin, cout
  Adder #(.width(32)) adder_2 (.a(out_10), .b(shifter_1_out), .out(adder_2_out));  // open: cin, cout
  Multiplexer #(.width(32), .enable("false")) multiplexer_1 (
    .in0(out_10), .in1(adder_2_out), .out(multiplexer_1_out), .sel(and_1_out));
  and and_1 (and_1_out, in_3, in_4);
  Comparator #(.width(32), .mode("unsigned")) comparator_1 (
    .a(PC_q), .b({32{1'b0}}), .eq(comparator_1_eq));  // open: gt, lt
  Multiplexer #(.width(32)) multiplexer_2 (
    .in0(multiplexer_1_out), .in1({PC[31:28], out_9[25:0], 2'b00}), .out(multiplexer_2_out), .sel(in_5));  // open: en
  // Probe on PC
  Multiplexer #(.width(32)) multiplexer_3 (.in0(PC_q), .in1(32'h3000), .out(PC), .sel(comparator_1_eq));  // open: en
  Multiplexer #(.width(32)) multiplexer_4 (.in0(multiplexer_2_out), .in1(in_8), .out(NPC), .sel(in_6));  // open: en
  // Probe on subtractor_1_out
  // Probe on subtractor_1_out[6:2]
  Subtractor #(.width(32)) subtractor_1 (.a(PC), .b(32'h3000), .out(subtractor_1_out));  // open: bin, bout
  // Probe on out_9
  ROM #(.addrWidth(5), .dataWidth(32)) rom_1 (.addr(subtractor_1_out[6:2]), .data(out_9));  // open: sel
  // Probe on out_9
  // Probe on {PC[31:28], out_9[25:0], 2'b00}

  // Other names for the same wires on the sheet: beq = in_3; clk = in_2; imm[31:0] = in_7; instr[31:0] = out_9;
  //   j_jal = in_5; jr = in_6; PC_4[31:0] = out_10; PC_j[31:2] = {PC[31:28], out_9[25:0]}; PC_jr[31:0] = in_8;
  //   Reset = in_1; Zero = in_4
endmodule
